# Fritzing sketch esp32-adc-ble-sensor-v2 (saved by Fritzing 0.9.3b)
# 18650 Li-ion Battery: CC-BY Dr Kristofer Chan, King's College London/Remote-research.org

parts:
  R1 = Resistor [tolerance=±10% resistance=4.7k package=THT]
  R2 = Resistor [tolerance=±5% resistance=22k package=THT]
  C1 = Ceramic Capacitor [capacitance=1mF package="200 mil [THT, multilayer]"]
  A2 = Esp32-c3 super mini
  OLED1 = OLED Mono 0.56 inch blue or white
  Q1 = NPN-Transistor [package="TO92 [THT]"]
  R3 = Resistor [tolerance=±5% resistance=4.7k package=THT]
  R4 = Resistor [tolerance=±5% resistance=10k package=THT]
  15V_2A = Power plug [part_number=Adaptor]
  15V_2A_2 = Power plug [part_number=Adaptor]
  18650 = 18650 Li-ion Battery [package=battery-18650]
  18650_2 = 18650 Li-ion Battery [package=battery-18650]
  18650_3 = 18650 Li-ion Battery [package=battery-18650]
  D1 = Schottky Diode [part_number=10SQ045 package="300 mil [THT]"]
  D2 = Schottky Diode [part_number=10SQ045 package="300 mil [THT]"]
  D3 = Schottky Diode [part_number=10SQ045 package="300 mil [THT]"]
  CHARGER = XL4015 DC-DC CC CV module (blue)
  DC-DC = XL4005 DC-DC
  RELAY = RELAY [package=relay-jzc]
  USB = USB Type A Female Breakout Board [part_number=Type-A]

nets:
  N1: R1.Pin_0, R2.Pin_1, A2.Pin_9
  GND: R1.Pin_1, C1.1, A2.Pin_15, OLED1.GND, Q1.E, R4.Pin_1, 15V_2A_2.GND, 18650.-, CHARGER.pin_4, DC-DC.IN-, DC-DC.OUT-, USB.GND
  N2: R2.Pin_0, 18650_3.+, D1.cathode, D3.anode
  N3: A2.Pin_2, OLED1.SDA
  N4: A2.Pin_3, OLED1.SCL
  N5: A2.Pin_7, R3.Pin_0
  N6: A2.Pin_14, OLED1.VCC
  N7: A2.Pin_16, DC-DC.OUT+, RELAY.MAIN, RELAY.COIL1
  N8: Q1.B, R3.Pin_1, R4.Pin_0
  N9: Q1.C, RELAY.COIL2
  N10: 15V_2A.GND, CHARGER.pin_2
  N11: 15V_2A.VCC, CHARGER.pin_1
  N12: 15V_2A_2.VCC, D2.anode
  N13: 18650.+, 18650_2.-
  N14: 18650_2.+, 18650_3.-
  N15: D1.anode, CHARGER.pin_3
  N16: D2.cathode, D3.cathode, DC-DC.IN+
  N17: RELAY.NO, USB.VCC

notes:
  12.9V 0.8A
  9-15V
  To Orange Pi 5V
  5V

custom parts:
  Esp32-c3 super mini: ESP32-C3 Development Board ESP32 SuperMini Development Board ESP32 Development Board WiFi Bluetooth.
  OLED Mono 0.56 inch blue or white: OLED, I2C 3.3V - 5V Blue and White text versions
  18650 Li-ion Battery: 18650 li-ion Battery Standard 18650 battery with interactive connectors Creative Common Attribution 4.0 International (CC-BY 4.0) license. Any use of this part requires attribution of Dr Kristofer Chan, Department of Geography, King's College London. Contact kristofer.chan [at] kcl.ac.uk OR kris [at] remote-research.org for further information.
  XL4015 DC-DC CC CV module (blue): XL4015 DC-DC CC/CV module blue
  XL4005 DC-DC: XL4005
  RELAY: SPDT relay (COM-00101)
  USB Type A Female Breakout Board: USB breakout board for a Type A connector. sparkfun.com
