# Fritzing sketch esp32-adc-ble-sensor-v3 (saved by Fritzing 0.9.3b)
# 18650 Li-ion Battery: CC-BY Dr Kristofer Chan, King's College London/Remote-research.org
circuit board: 8.46667cm x 5.64444cm

parts:
  R1 = Resistor [tolerance=±10% resistance=4.7k package=THT]
  R2 = Resistor [tolerance=±5% resistance=22k package=THT]
  C1 = Ceramic Capacitor [capacitance=1mF package="200 mil [THT, multilayer]"]
  CPU = Esp32-c3 super mini
  15V_2A = Power plug [part_number="Adaptor 1"]
  18650 = 18650 Li-ion Battery [package=battery-18650]
  18650_2 = 18650 Li-ion Battery [package=battery-18650]
  18650_3 = 18650 Li-ion Battery [package=battery-18650]
  D1 = Schottky Diode [part_number=10SQ045 package="300 mil [THT]"]
  D2 = Schottky Diode [part_number=10SQ045 package="300 mil [THT]"]
  D3 = Schottky Diode [part_number=10SQ045 package="300 mil [THT]"]
  USB = USB Type A Female Breakout Board [part_number=Type-A]
  RELAY = KY-019 5V Relay Module [package="Breakout board"]
  15V_2A_2 = Power plug [part_number="Adaptor 2"]
  DC-DC = XL4005 DC-DC
  CHARGER = XL4015 DC-DC CC CV module (blue)
  C2 = Ceramic Capacitor [capacitance=1mF package="200 mil [THT, multilayer]"]
  R3 = Resistor [tolerance=±10% resistance=4.7k package=THT]
  R4 = Resistor [tolerance=±5% resistance=22k package=THT]
  BMS-3S_10A = 3S-BMS

nets:
  N1: R1.Pin_0, R2.Pin_1, C1.0, CPU.Pin_9
  GND: R1.Pin_1, C1.1, CPU.Pin_15, USB.GND, RELAY.-, 15V_2A_2.GND, DC-DC.IN-, DC-DC.OUT-, CHARGER.pin_4, C2.0, R3.Pin_0, BMS-3S_10A.-
  N2: R2.Pin_0, D1.cathode, D3.anode, BMS-3S_10A.+
  N3: CPU.Pin_7, RELAY.S
  N4: CPU.Pin_10, C2.1, R3.Pin_1, R4.Pin_0
  N5: CPU.Pin_16, RELAY.+, RELAY.Common, DC-DC.OUT+
  N6: 15V_2A.GND, CHARGER.pin_2
  N7: 15V_2A.VCC, CHARGER.pin_1
  N8: 18650.-, BMS-3S_10A.0V
  N9: 18650.+, 18650_2.-, BMS-3S_10A.4.2V
  N10: 18650_2.+, 18650_3.-, BMS-3S_10A.8.4V
  N11: 18650_3.+, BMS-3S_10A.12.6V
  N12: D1.anode, CHARGER.pin_3, R4.Pin_1
  N13: D2.cathode, D3.cathode, DC-DC.IN+
  N14: D2.anode, 15V_2A_2.VCC
  N15: USB.VCC, RELAY.NO

notes:
  12.9V 0.8A
  9-15V
  To Orange Pi 5V
  5V
  https://github.com/AlexVakhnin/ESP32-C3-ADC-BLE-SENSOR

custom parts:
  Esp32-c3 super mini: ESP32-C3 Development Board ESP32 SuperMini Development Board ESP32 Development Board WiFi Bluetooth.
  18650 Li-ion Battery: 18650 li-ion Battery Standard 18650 battery with interactive connectors Creative Common Attribution 4.0 International (CC-BY 4.0) license. Any use of this part requires attribution of Dr Kristofer Chan, Department of Geography, King's College London. Contact kristofer.chan [at] kcl.ac.uk OR kris [at] remote-research.org for further information.
  USB Type A Female Breakout Board: USB breakout board for a Type A connector. sparkfun.com
  KY-019 5V Relay Module: KY-019 5V Relay module, used to control AC circuits. (Special thanks to vanepp for fixing the PCB holes and other errors)
  XL4005 DC-DC: XL4005
  XL4015 DC-DC CC CV module (blue): XL4015 DC-DC CC/CV module blue
  3S-BMS: 3S-BMS LIPO battery charger / protection unit. Note pcb does not match the board as it will likely connect with wires, so pcb is 6 pads suitable for .1in header pins.
