# Fritzing sketch esp32-adc-ble-sensor (saved by Fritzing 0.9.3b)

parts:
  U1 = SBX DSUN [part_number=MP1584 package=THT]
  R1 = Resistor [tolerance=±10% resistance=4.7k package=THT]
  R2 = Resistor [tolerance=±5% resistance=22k package=THT]
  C1 = Ceramic Capacitor [capacitance=1mF package="200 mil [THT, multilayer]"]
  A2 = Esp32-c3 super mini
  BAT1 = 12 battery [part_number="12V 40Ah" package=battery]
  OLED1 = OLED Mono 0.56 inch blue or white

nets:
  GND: U1.GND, R1.Pin_1, C1.1, A2.Pin_15, BAT1.-, OLED1.GND
  N1: U1.+VIN, R2.Pin_0, BAT1.+
  N2: U1.+VOUT, A2.Pin_16
  N3: R1.Pin_0, R2.Pin_1, A2.Pin_9
  N4: A2.Pin_2, OLED1.SDA
  N5: A2.Pin_3, OLED1.SCL
  N6: A2.Pin_14, OLED1.VCC

custom parts:
  SBX DSUN: SBX DSUN input voltage 4.5 - 28V DC output voltage .8v to 20VDC (step down converter) Output current 3A max
  Esp32-c3 super mini: ESP32-C3 Development Board ESP32 SuperMini Development Board ESP32 Development Board WiFi Bluetooth.
  12 battery: 12V lead acid type battery, like the Husqvarna YTH2448 12V 35AH battery. This is the mini version 1/4 the size of the actual battery to be closer to typical breadboard parts (around 2in wide rathher than 7in). The pads in pcb are sized to accomidate up to 14ga wire (as these batterys will deliver high currents.)
  OLED Mono 0.56 inch blue or white: OLED, I2C 3.3V - 5V Blue and White text versions
